// Logisim project Sadat Parvej_SAP-1_Circuit.circ as structural Verilog: 22 circuits, main circuit main
module main (
  output [3:0] LSB,
  output [3:0] MSB,
  output [3:0] out_3,
  output [3:0] out_4
);

  wire CE_prime, CLK, clock_1_out, CLR, CLR_out, Cp, EA, Ei_prime, Ep, Eu, HLT_prime, LA_prime, LB_prime,
       Li_prime, LM_prime, Lo_prime, not_1_out, Su;
  wire [3:0] A3_A0, A7_A4, B3_B0, B7_B4, IR_OUT_MSB, MAR_OUT;

  CONTROLLER controller_1 (
    .in_1(CLK), .in_2(CLR), .I7_I4(IR_OUT_MSB), .out_4(HLT_prime), .out_5(Cp), .out_6(Ep), .out_7(LM_prime),
    .out_8(CE_prime), .out_9(Li_prime), .out_10(Ei_prime), .out_11(LA_prime), .out_12(EA), .out_13(Su),
    .out_14(Eu), .out_15(LB_prime), .out_16(Lo_prime));
  prog__counter prog_counter_1 (.in_1(Cp), .in_2(CLK), .in_3(CLR), .in_4(Ep), .out_5(LSB));
  MAR mar_1 (
    .in_1(LSB[0]), .in_2(LSB[1]), .in_3(LSB[2]), .in_4(LSB[3]), .in_5(LM_prime), .in_6(CLK), .in_7(CLR),
    .out_8(MAR_OUT));
  Button u_CLR (.out(CLR_out));
  not not_1 (not_1_out, CE_prime);
  Instruction_Register instruction_register_1 (
    .in_3(Li_prime), .in_4(CLK), .in_5(CLR), .out_7(LSB), .out_8(IR_OUT_MSB), .in_1(LSB), .in_2(MSB),
    .in_6(Ei_prime));
  RAM #(.addrWidth(4)) ram_1 (.addr(MAR_OUT), .data({MSB, LSB}), .ld(not_1_out), .clr(CLR_out));  // open: sel, clk
  Button button_1 (.out(CLR));
  Adder_Subtractor adder_subtractor_1 (
    .Su(Su), .B3B2B1B0(B3_B0), .A3A2A1A0(A3_A0), .B7B6B5B4(B7_B4), .A7A6A5A4(A7_A4), .out_7(LSB),
    .out_8(MSB), .in_6(Eu));  // open: out_9
  Accumulator_A accumulator_a_1 (
    .in_1(LSB), .in_2(MSB), .in_3(LA_prime), .in_4(CLK), .in_5(CLR), .in_6(EA), .out_7(LSB), .out_8(MSB),
    .out_9(A3_A0), .out_10(A7_A4));
  Register_B register_b_1 (
    .in_1(LSB), .in_2(MSB), .in_3(LB_prime), .in_4(CLK), .in_5(CLR), .out_6(B3_B0), .out_7(B7_B4));
  output_register output_register_1 (
    .in_1(LSB), .in_2(MSB), .in_3(Lo_prime), .in_4(CLK), .out_6(out_3), .out_7(out_4), .in_5(CLR));
  assign CLK = HLT_prime ? clock_1_out : 1'bz;  // Controlled_Buffer controlled_buffer_1
  Clock clock_1 (.out(clock_1_out));
  Hex_Digit_Display hex_digit_display_1 (.value(out_4));  // open: dp
  Hex_Digit_Display hex_digit_display_2 (.value(out_3));  // open: dp

  // Other names for the same wires on the sheet: A_IN_LSB[3:0] = LSB; A_OUT_LSB[3:0] = LSB; B_IN_LSB[3:0] = LSB;
  //   IR_IN_LSB[3:0] = LSB; IR_OUT_LSB[3:0] = LSB; MAR_IN[3:0] = LSB; O_IN_LSB[3:0] = LSB; PC_OUT[3:0] = LSB;
  //   RAM_OUT_LSB[3:0] = LSB; S3_S0[3:0] = LSB; A_IN_MSB[3:0] = MSB; A_OUT_MSB[3:0] = MSB; B_IN_MSB[3:0] = MSB;
  //   IR_IN_MSB[3:0] = MSB; O_IN_MSB[3:0] = MSB; RAM_OUT_MSB[3:0] = MSB; S7_S4[3:0] = MSB; O_OUT_LSB[3:0] = out_3;
  //   O_OUT_MSB[3:0] = out_4

  // Notes on the sheet:
  //   RAM
  //   OUTPUT
endmodule

module MAR (
  input  in_1,
  input  in_2,
  input  in_3,
  input  in_4,
  input  in_5,
  input  in_6,
  input  in_7,
  output [3:0] out_8
);

  wire not_1_out;

  not not_1 (not_1_out, in_5);
  Register #(.width(4)) register_1 (.D({in_4, in_3, in_2, in_1}), .en(not_1_out), .Q(out_8), .clk(in_6), .clr(in_7));
endmodule

module prog__counter (
  input  in_1,
  input  in_2,
  input  in_3,
  input  in_4,
  output [3:0] out_5
);

  wire [3:0] counter_1_q;

  Counter #(.width(4), .max('hf)) counter_1 (
    .count(in_1), .Q(counter_1_q), .clk(in_2), .clr(in_3));  // open: load, D, carry
  assign out_5 = in_4 ? counter_1_q : 4'bz;  // Controlled_Buffer controlled_buffer_1
endmodule

module Instruction_Register (
  input  [3:0] in_1,
  input  [3:0] in_2,
  input  in_3,
  input  in_4,
  input  in_5,
  input  in_6,
  output [3:0] out_7,
  output [3:0] out_8
);

  wire not_1_out, not_2_out;
  wire [3:0] register_1_q;

  not not_1 (not_1_out, in_3);
  not not_2 (not_2_out, in_6);
  Register #(.trigger("falling")) register_1 (
    .D({in_2, in_1}), .en(not_1_out), .Q({out_8, register_1_q}), .clk(in_4), .clr(in_5));
  assign out_7 = not_2_out ? register_1_q : 4'bz;  // Controlled_Buffer controlled_buffer_1
endmodule

module output_register (
  input  [3:0] in_1,
  input  [3:0] in_2,
  input  in_3,
  input  in_4,
  input  in_5,
  output [3:0] out_6,
  output [3:0] out_7
);

  wire not_1_out;

  not not_1 (not_1_out, in_3);
  Register register_1 (.D({in_2, in_1}), .en(not_1_out), .Q({out_7, out_6}), .clk(in_4), .clr(in_5));
endmodule

module Register_B (
  input  [3:0] in_1,
  input  [3:0] in_2,
  input  in_3,
  input  in_4,
  input  in_5,
  output [3:0] out_6,
  output [3:0] out_7
);

  wire not_1_out;

  not not_1 (not_1_out, in_3);
  Register register_1 (.D({in_2, in_1}), .en(not_1_out), .Q({out_7, out_6}), .clk(in_4), .clr(in_5));
endmodule

module Accumulator_A (
  input  [3:0] in_1,
  input  [3:0] in_2,
  input  in_3,
  input  in_4,
  input  in_5,
  input  in_6,
  output [3:0] out_7,
  output [3:0] out_8,
  output [3:0] out_9,
  output [3:0] out_10
);

  wire not_1_out;

  not not_1 (not_1_out, in_3);
  Register register_1 (.D({in_2, in_1}), .en(not_1_out), .Q({out_10, out_9}), .clk(in_4), .clr(in_5));
  assign {out_8, out_7} = in_6 ? {out_10, out_9} : 8'bz;  // Controlled_Buffer controlled_buffer_1
endmodule

module Adder_Subtractor (
  input  Su,
  input  [3:0] B3B2B1B0,
  input  [3:0] A3A2A1A0,
  input  [3:0] B7B6B5B4,
  input  [3:0] A7A6A5A4,
  input  in_6,
  output [3:0] out_7,
  output [3:0] out_8,
  output out_9
);

  wire adder_1_cout, adder_2_cout, adder_3_cout, adder_4_cout, adder_5_cout, adder_6_cout, adder_7_cout,
       xor_1_out, xor_2_out, xor_3_out, xor_4_out, xor_5_out, xor_6_out, xor_7_out, xor_8_out;
  wire [3:0] adder_1_out, adder_5_out;

  xor xor_1 (xor_1_out, B3B2B1B0[0], Su);
  xor xor_2 (xor_2_out, B3B2B1B0[1], Su);
  xor xor_3 (xor_3_out, B3B2B1B0[2], Su);
  xor xor_4 (xor_4_out, B3B2B1B0[3], Su);
  xor xor_5 (xor_5_out, B7B6B5B4[0], Su);
  xor xor_6 (xor_6_out, B7B6B5B4[1], Su);
  xor xor_7 (xor_7_out, B7B6B5B4[2], Su);
  xor xor_8 (xor_8_out, B7B6B5B4[3], Su);
  Adder #(.width(1)) adder_1 (.a(A3A2A1A0[0]), .b(xor_1_out), .out(adder_1_out[0]), .cin(Su), .cout(adder_1_cout));
  Adder #(.width(1)) adder_2 (
    .a(A3A2A1A0[1]), .b(xor_2_out), .out(adder_1_out[1]), .cin(adder_1_cout), .cout(adder_2_cout));
  Adder #(.width(1)) adder_3 (
    .a(A3A2A1A0[2]), .b(xor_3_out), .out(adder_1_out[2]), .cin(adder_2_cout), .cout(adder_3_cout));
  Adder #(.width(1)) adder_4 (
    .a(A3A2A1A0[3]), .b(xor_4_out), .out(adder_1_out[3]), .cin(adder_3_cout), .cout(adder_4_cout));
  Adder #(.width(1)) adder_5 (
    .a(A7A6A5A4[0]), .b(xor_5_out), .out(adder_5_out[0]), .cin(adder_4_cout), .cout(adder_5_cout));
  Adder #(.width(1)) adder_6 (
    .a(A7A6A5A4[1]), .b(xor_6_out), .out(adder_5_out[1]), .cin(adder_5_cout), .cout(adder_6_cout));
  Adder #(.width(1)) adder_7 (
    .a(A7A6A5A4[2]), .b(xor_7_out), .out(adder_5_out[2]), .cin(adder_6_cout), .cout(adder_7_cout));
  Adder #(.width(1)) adder_8 (.a(A7A6A5A4[3]), .b(xor_8_out), .out(adder_5_out[3]), .cin(adder_7_cout), .cout(out_9));
  assign {out_8, out_7} = in_6 ? {adder_5_out, adder_1_out} : 8'bz;  // Controlled_Buffer controlled_buffer_1

  // Notes on the sheet:
  //   S0
  //   S1
  //   S2
  //   S3
  //   S4
  //   S5
  //   S6
  //   S7
endmodule

module Instruction_Decoder (
  input  [3:0] I7_I6_I5_I4,
  output LDA,
  output ADD,
  output SUB,
  output OUT,
  output HLT
);

  wire nand_1_out, nand_2_out, nand_3_out, nand_4_out, nand_5_out, nand_6_out, nand_7_out, nand_8_out,
       nand_9_out, nand_10_out, nand_11_out, nand_12_out, nand_13_out, nand_14_out, nand_15_out, nand_16_out,
       nand_17_out, nand_18_out, nand_19_out, nand_20_out, nand_21_out, nand_22_out, nand_23_out,
       nand_24_out, nand_25_out, nand_26_out, nand_27_out, nand_28_out, nand_29_out, nand_30_out,
       nand_31_out, nand_32_out, nand_33_out, nand_34_out, nand_35_out, nand_36_out;

  nand nand_1 (nand_1_out, I7_I6_I5_I4[3], I7_I6_I5_I4[3]);
  nand nand_2 (nand_2_out, I7_I6_I5_I4[2], I7_I6_I5_I4[2]);
  nand nand_3 (nand_3_out, I7_I6_I5_I4[1], I7_I6_I5_I4[1]);
  nand nand_4 (nand_4_out, I7_I6_I5_I4[0], I7_I6_I5_I4[0]);
  nand nand_5 (nand_5_out, I7_I6_I5_I4[3], I7_I6_I5_I4[3]);
  nand nand_6 (nand_6_out, I7_I6_I5_I4[2], I7_I6_I5_I4[2]);
  nand nand_7 (nand_7_out, I7_I6_I5_I4[1], I7_I6_I5_I4[1]);
  nand nand_8 (nand_8_out, I7_I6_I5_I4[3], I7_I6_I5_I4[3]);
  nand nand_9 (nand_9_out, I7_I6_I5_I4[2], I7_I6_I5_I4[2]);
  nand nand_10 (nand_10_out, I7_I6_I5_I4[0], I7_I6_I5_I4[0]);
  nand nand_11 (nand_11_out, I7_I6_I5_I4[0], I7_I6_I5_I4[0]);
  nand nand_12 (nand_12_out, I7_I6_I5_I4[3], I7_I6_I5_I4[2]);
  nand nand_13 (nand_13_out, I7_I6_I5_I4[1], I7_I6_I5_I4[0]);
  nand nand_14 (nand_14_out, nand_1_out, nand_2_out);
  nand nand_15 (nand_15_out, nand_3_out, nand_4_out);
  nand nand_16 (nand_16_out, nand_5_out, nand_6_out);
  nand nand_17 (nand_17_out, nand_7_out, I7_I6_I5_I4[0]);
  nand nand_18 (nand_18_out, nand_8_out, nand_9_out);
  nand nand_19 (nand_19_out, I7_I6_I5_I4[1], nand_10_out);
  nand nand_20 (nand_20_out, I7_I6_I5_I4[3], I7_I6_I5_I4[2]);
  nand nand_21 (nand_21_out, I7_I6_I5_I4[1], nand_11_out);
  nand nand_22 (nand_22_out, nand_12_out, nand_12_out);
  nand nand_23 (nand_23_out, nand_13_out, nand_13_out);
  nand nand_24 (nand_24_out, nand_14_out, nand_14_out);
  nand nand_25 (nand_25_out, nand_15_out, nand_15_out);
  nand nand_26 (nand_26_out, nand_16_out, nand_16_out);
  nand nand_27 (nand_27_out, nand_17_out, nand_17_out);
  nand nand_28 (nand_28_out, nand_18_out, nand_18_out);
  nand nand_29 (nand_29_out, nand_19_out, nand_19_out);
  nand nand_30 (nand_30_out, nand_20_out, nand_20_out);
  nand nand_31 (nand_31_out, nand_21_out, nand_21_out);
  nand nand_32 (nand_32_out, nand_22_out, nand_23_out);
  nand nand_33 (nand_33_out, nand_24_out, nand_25_out);
  nand nand_34 (nand_34_out, nand_26_out, nand_27_out);
  nand nand_35 (nand_35_out, nand_28_out, nand_29_out);
  nand nand_36 (nand_36_out, nand_30_out, nand_31_out);
  nand nand_37 (HLT, nand_32_out, nand_32_out);
  nand nand_38 (LDA, nand_33_out, nand_33_out);
  nand nand_39 (ADD, nand_34_out, nand_34_out);
  nand nand_40 (SUB, nand_35_out, nand_35_out);
  nand nand_41 (OUT, nand_36_out, nand_36_out);
endmodule

module Ring_Counter (
  input  CLK,
  input  CLR,
  output T1,
  output T2,
  output T3,
  output T4,
  output T5,
  output T6
);

  wire nor_1_out;

  nor nor_1 (nor_1_out, T1, T2, T3, T4, T5, T6);
  D_Flip_Flop D1 (.clk(CLK), .D(nor_1_out), .Q(T1), .reset(CLR));  // open: Qn, preset, en
  D_Flip_Flop d_ff_1 (.clk(CLK), .D(T1), .Q(T2), .reset(CLR));  // open: Qn, preset, en
  D_Flip_Flop d_ff_2 (.clk(CLK), .D(T2), .Q(T3), .reset(CLR));  // open: Qn, preset, en
  D_Flip_Flop d_ff_3 (.clk(CLK), .D(T3), .Q(T4), .reset(CLR));  // open: Qn, preset, en
  D_Flip_Flop d_ff_4 (.clk(CLK), .D(T4), .Q(T5), .reset(CLR));  // open: Qn, preset, en
  D_Flip_Flop d_ff_5 (.clk(CLK), .D(T5), .Q(T6), .reset(CLR));  // open: Qn, preset, en
endmodule

module Testing_Field (
  input  in_1,
  input  [3:0] in_2,
  input  in_3,
  output out_4,
  output [3:0] out_5,
  output [3:0] out_6,
  output [3:0] out_7,
  output [3:0] out_8,
  output [3:0] out_9,
  output [3:0] out_10,
  output [3:0] out_11,
  output [3:0] out_12
);

  wire CE_prime, Cp, EA, Ei_prime, Ep, Eu, LA_prime, LB_prime, Li_prime, LM_prime, Lo_prime, Su;
  wire [3:0] accumulator_a_1_out_9, accumulator_a_1_out_10;

  CONTROLLER_1 controller_1_1 (
    .in_1(in_3), .in_2(in_1), .I7_I4(in_2), .Cp(Cp), .Ep(Ep), .LM_prime(LM_prime), .CE_prime(CE_prime),
    .Li_prime(Li_prime), .Ei_prime(Ei_prime), .LA_prime(LA_prime), .EA(EA), .Su(Su), .Eu(Eu),
    .LB_prime(LB_prime), .Lo_prime(Lo_prime), .HLT_prime(out_4));
  Adder_Subtractor adder_subtractor_1 (
    .Su(Su), .B3B2B1B0(out_9), .A3A2A1A0(accumulator_a_1_out_9), .B7B6B5B4(out_10),
    .A7A6A5A4(accumulator_a_1_out_10), .out_7(out_5), .out_8(out_6), .in_6(Eu));  // open: out_9
  Accumulator_A accumulator_a_1 (
    .in_1(out_5), .in_2(out_6), .in_3(LA_prime), .in_4(in_3), .in_6(EA), .out_7(out_5), .out_8(out_6),
    .out_9(accumulator_a_1_out_9), .out_10(accumulator_a_1_out_10));  // open: in_5
  Register_B register_b_1 (
    .in_1(out_5), .in_2(out_6), .in_3(LB_prime), .in_4(in_3), .out_6(out_9), .out_7(out_10));  // open: in_5
  output_register output_register_1 (
    .in_1(out_5), .in_2(out_6), .in_3(Lo_prime), .in_4(in_3), .out_6(out_11), .out_7(out_12));  // open: in_5

  assign out_7 = out_6;
  assign out_8 = out_5;

  // Other names for the same wires on the sheet: CLK = in_3
endmodule

module CONTROLLER_1 (
  input  in_1,
  input  in_2,
  input  [3:0] I7_I4,
  output HLT_prime,
  output Cp,
  output Ep,
  output LM_prime,
  output CE_prime,
  output Li_prime,
  output Ei_prime,
  output LA_prime,
  output EA,
  output Su,
  output Eu,
  output LB_prime,
  output Lo_prime
);

  wire and_1_out, and_2_out, and_3_out, and_4_out, and_5_out, and_6_out, and_7_out, and_8_out, and_9_out,
       and_10_out, and_11_out, and_12_out, and_13_out, and_14_out, and_15_out, and_16_out,
       instruction_decoder_1_add, instruction_decoder_1_hlt, instruction_decoder_1_lda,
       instruction_decoder_1_out, instruction_decoder_1_sub, nand_1_out, nand_2_out, or_1_out, or_2_out,
       or_3_out, or_4_out, or_6_out, T3, T4, T5, T6;

  Ring_Counter ring_counter_1 (.CLK(in_1), .CLR(in_2), .T1(Ep), .T2(Cp), .T3(T3), .T4(T4), .T5(T5), .T6(T6));
  Instruction_Decoder instruction_decoder_1 (
    .I7_I6_I5_I4(I7_I4), .LDA(instruction_decoder_1_lda), .ADD(instruction_decoder_1_add),
    .SUB(instruction_decoder_1_sub), .OUT(instruction_decoder_1_out), .HLT(instruction_decoder_1_hlt));
  not not_1 (HLT_prime, instruction_decoder_1_hlt);
  and and_1 (and_1_out, instruction_decoder_1_lda, T4);
  or or_1 (or_1_out, Ep, and_1_out, and_2_out, and_3_out);
  not not_2 (LM_prime, or_1_out);
  and and_2 (and_2_out, instruction_decoder_1_add, T4);
  and and_3 (and_3_out, instruction_decoder_1_sub, T4);
  and and_4 (and_4_out, instruction_decoder_1_lda, T5);
  or or_2 (or_2_out, T3, and_4_out, and_5_out, and_6_out);
  not not_3 (CE_prime, or_2_out);
  and and_5 (and_5_out, instruction_decoder_1_add, T5);
  and and_6 (and_6_out, instruction_decoder_1_sub, T5);
  not not_4 (Li_prime, T3);
  and and_7 (and_7_out, instruction_decoder_1_lda, T4);
  or or_3 (or_3_out, and_7_out, and_9_out, and_8_out);
  not not_5 (Ei_prime, or_3_out);
  and and_8 (and_8_out, instruction_decoder_1_sub, T4);
  and and_9 (and_9_out, instruction_decoder_1_add, T4);
  and and_10 (and_10_out, instruction_decoder_1_lda, T5);
  or or_4 (or_4_out, and_10_out, and_12_out, and_11_out);
  not not_6 (LA_prime, or_4_out);
  and and_11 (and_11_out, instruction_decoder_1_sub, T6);
  and and_12 (and_12_out, instruction_decoder_1_add, T6);
  nand nand_1 (nand_1_out, instruction_decoder_1_out, T4);
  not not_7 (EA, nand_1_out);
  nand nand_2 (nand_2_out, instruction_decoder_1_sub, T6);
  not not_8 (Su, nand_2_out);
  and and_13 (and_13_out, instruction_decoder_1_sub, T6);
  and and_14 (and_14_out, instruction_decoder_1_add, T6);
  or or_5 (Eu, and_14_out, and_13_out);
  and and_15 (and_15_out, instruction_decoder_1_add, T5);
  and and_16 (and_16_out, instruction_decoder_1_sub, T5);
  or or_6 (or_6_out, and_15_out, and_16_out);
  not not_9 (LB_prime, or_6_out);
  nand nand_3 (Lo_prime, instruction_decoder_1_out, T4);

  // Other names for the same wires on the sheet: T1 = Ep; T2 = Cp
endmodule

module sap_building_1_1 (
  input  in_1,
  input  in_2,
  input  in_3,
  output [3:0] out_4,
  output [3:0] out_5,
  output [3:0] out_6,
  output [3:0] out_7,
  output [3:0] out_8,
  output [3:0] out_9,
  output [3:0] out_10,
  output [3:0] out_11,
  output [3:0] out_12,
  output [3:0] out_13,
  output [3:0] out_14,
  output [3:0] out_15,
  output [3:0] out_16,
  output [3:0] out_17,
  output [3:0] out_18,
  output [3:0] out_19,
  output out_20
);

  wire CE_prime, Cp, EA, Ei_prime, Ep, Eu, LA_prime, LB_prime, Li_prime, LM_prime, Lo_prime, not_1_out, Su;
  wire [3:0] accumulator_a_1_out_9, accumulator_a_1_out_10;

  not not_1 (not_1_out, CE_prime);
  CONTROLLER_1 controller_1_1 (
    .in_1(in_2), .in_2(in_3), .I7_I4(out_16), .Cp(Cp), .Ep(Ep), .LM_prime(LM_prime), .CE_prime(CE_prime),
    .Li_prime(Li_prime), .Ei_prime(Ei_prime), .LA_prime(LA_prime), .EA(EA), .Su(Su), .Eu(Eu),
    .LB_prime(LB_prime), .Lo_prime(Lo_prime), .HLT_prime(out_20));
  prog__counter prog_counter_1 (.in_1(Cp), .in_2(in_2), .in_3(in_3), .in_4(Ep), .out_5(out_4));
  // MAR mar_1: pin names not known; wires that end beside it: out_4[0], out_4[1], out_4[2], out_4[3], LM_prime, in_2, in_3, out_7
  RAM #(.addrWidth(4)) ram_1 (.addr(out_7), .data({out_5, out_4}), .ld(not_1_out), .clr(in_1));  // open: sel, clk
  Instruction_Register instruction_register_1 (
    .in_3(Li_prime), .in_4(in_2), .in_5(in_3), .out_7(out_4), .out_8(out_16), .in_1(out_4), .in_2(out_5),
    .in_6(Ei_prime));
  Accumulator_A accumulator_a_1 (
    .in_1(out_4), .in_2(out_5), .in_3(LA_prime), .in_4(in_2), .in_6(EA), .out_7(out_4), .out_8(out_5),
    .out_9(accumulator_a_1_out_9), .out_10(accumulator_a_1_out_10));  // open: in_5
  Adder_Subtractor adder_subtractor_1 (
    .Su(Su), .B3B2B1B0(out_13), .A3A2A1A0(accumulator_a_1_out_9), .B7B6B5B4(out_14),
    .A7A6A5A4(accumulator_a_1_out_10), .out_7(out_4), .out_8(out_5), .in_6(Eu));  // open: out_9
  Register_B register_b_1 (
    .in_1(out_4), .in_2(out_5), .in_3(LB_prime), .in_4(in_2), .out_6(out_13), .out_7(out_14));  // open: in_5
  output_register output_register_1 (
    .in_1(out_4), .in_2(out_5), .in_3(Lo_prime), .in_4(in_2), .out_6(out_18), .out_7(out_19));  // open: in_5

  assign out_6 = out_4;
  assign out_8 = out_5;
  assign out_9 = out_4;
  assign out_10 = out_4;
  assign out_11 = out_5;
  assign out_12 = out_5;
  assign out_15 = out_4;
  assign out_17 = out_4;

  // Other names for the same wires on the sheet: CLK = in_2; CLR = in_3

  // Notes on the sheet:
  //   MSB
  //   LSB
endmodule

module Ring_counter_1_1 (
  input  CLK,
  input  CLR,
  output T1,
  output T2,
  output T3,
  output T4,
  output T5,
  output T6
);

  wire j_k_ff_1_q, j_k_ff_2_qn, j_k_ff_3_qn, j_k_ff_4_qn, j_k_ff_5_qn, j_k_ff_6_qn, not_1_out;

  not not_1 (not_1_out, CLK);
  J_K_Flip_Flop j_k_ff_1 (
    .J(j_k_ff_6_qn), .clk(not_1_out), .K(T6), .Q(j_k_ff_1_q), .Qn(T1), .reset(CLR));  // open: preset, en
  J_K_Flip_Flop j_k_ff_2 (
    .J(T1), .clk(not_1_out), .K(j_k_ff_1_q), .Q(T2), .Qn(j_k_ff_2_qn), .reset(CLR));  // open: preset, en
  J_K_Flip_Flop j_k_ff_3 (
    .J(T2), .clk(not_1_out), .K(j_k_ff_2_qn), .Q(T3), .Qn(j_k_ff_3_qn), .reset(CLR));  // open: preset, en
  J_K_Flip_Flop j_k_ff_4 (
    .J(T3), .clk(not_1_out), .K(j_k_ff_3_qn), .Q(T4), .Qn(j_k_ff_4_qn), .reset(CLR));  // open: preset, en
  J_K_Flip_Flop j_k_ff_5 (
    .J(T4), .clk(not_1_out), .K(j_k_ff_4_qn), .Q(T5), .Qn(j_k_ff_5_qn), .reset(CLR));  // open: preset, en
  J_K_Flip_Flop j_k_ff_6 (
    .J(T5), .clk(not_1_out), .K(j_k_ff_5_qn), .Q(T6), .Qn(j_k_ff_6_qn), .reset(CLR));  // open: preset, en
endmodule

module sap_building_1_2_working (
  input  in_1,
  input  in_2,
  input  in_3,
  output [3:0] out_4,
  output [3:0] out_5,
  output [3:0] out_6,
  output [3:0] out_7,
  output [3:0] out_8,
  output [3:0] out_9,
  output [3:0] out_10,
  output [3:0] out_11,
  output [3:0] out_12,
  output [3:0] out_13,
  output [3:0] out_14,
  output [3:0] out_15,
  output [3:0] out_16,
  output [3:0] out_17,
  output [3:0] out_18,
  output [3:0] out_19
);

  wire CE_prime, Cp, EA, Ei_prime, Ep, Eu, HLT_prime, LA_prime, LB_prime, Li_prime, LM_prime, Lo_prime,
       not_1_out, Su;
  wire [3:0] accumulator_a_1_out_9, accumulator_a_1_out_10;

  CONTROLLER controller_1 (
    .in_1(in_2), .in_2(in_3), .I7_I4(out_16), .out_4(HLT_prime), .out_5(Cp), .out_6(Ep), .out_7(LM_prime),
    .out_8(CE_prime), .out_9(Li_prime), .out_10(Ei_prime), .out_11(LA_prime), .out_12(EA), .out_13(Su),
    .out_14(Eu), .out_15(LB_prime), .out_16(Lo_prime));
  not not_1 (not_1_out, CE_prime);
  prog__counter prog_counter_1 (.in_1(Cp), .in_2(in_2), .in_3(in_3), .in_4(Ep), .out_5(out_4));
  MAR mar_1 (
    .in_1(out_4[0]), .in_2(out_4[1]), .in_3(out_4[2]), .in_4(out_4[3]), .in_5(LM_prime), .in_6(in_2),
    .in_7(in_3), .out_8(out_7));
  RAM #(.addrWidth(4)) ram_1 (.addr(out_7), .data({out_5, out_4}), .ld(not_1_out), .clr(in_1));  // open: sel, clk
  Instruction_Register instruction_register_1 (
    .in_3(Li_prime), .in_4(in_2), .in_5(in_3), .out_7(out_4), .out_8(out_16), .in_1(out_4), .in_2(out_5),
    .in_6(Ei_prime));
  Accumulator_A accumulator_a_1 (
    .in_1(out_4), .in_2(out_5), .in_3(LA_prime), .in_4(in_2), .in_6(EA), .out_7(out_4), .out_8(out_5),
    .out_9(accumulator_a_1_out_9), .out_10(accumulator_a_1_out_10));  // open: in_5
  Adder_Subtractor adder_subtractor_1 (
    .Su(Su), .B3B2B1B0(out_13), .A3A2A1A0(accumulator_a_1_out_9), .B7B6B5B4(out_14),
    .A7A6A5A4(accumulator_a_1_out_10), .out_7(out_4), .out_8(out_5), .in_6(Eu));  // open: out_9
  Register_B register_b_1 (
    .in_1(out_4), .in_2(out_5), .in_3(LB_prime), .in_4(in_2), .out_6(out_13), .out_7(out_14));  // open: in_5
  output_register output_register_1 (
    .in_1(out_4), .in_2(out_5), .in_3(Lo_prime), .in_4(in_2), .out_6(out_18), .out_7(out_19));  // open: in_5

  assign out_6 = out_4;
  assign out_8 = out_5;
  assign out_9 = out_4;
  assign out_10 = out_4;
  assign out_11 = out_5;
  assign out_12 = out_5;
  assign out_15 = out_4;
  assign out_17 = out_4;

  // Other names for the same wires on the sheet: CLK = in_2; CLR = in_3

  // Notes on the sheet:
  //   MSB
  //   LSB
endmodule

module Testing_Field_2 (
  input  in_1,
  input  in_2,
  input  in_3,
  input  [7:0] in_4,
  input  in_5,
  input  in_6,
  input  in_7,
  input  in_8,
  input  in_9,
  output [3:0] PC_OUT,
  output [3:0] MAR_IN,
  output [3:0] MAR_OUT,
  output [3:0] MSB,
  output [3:0] LSB,
  output [3:0] MSB_2,
  output [3:0] LSB_2,
  output [3:0] MSB_3,
  output [3:0] LSB_3,
  output out_19
);

  wire CE_prime, Cp, EA, Ei_prime, Ep, Eu, LA_prime, LB_prime, Li_prime, LM_prime, Lo_prime, not_1_out, Su;

  not not_1 (not_1_out, CE_prime);
  prog__counter prog_counter_1 (.in_1(Cp), .in_2(in_1), .in_3(in_2), .in_4(Ep), .out_5(LSB));
  MAR mar_1 (
    .in_1(LSB[0]), .in_2(LSB[1]), .in_3(LSB[2]), .in_4(LSB[3]), .in_5(LM_prime), .in_6(in_1), .in_7(in_3),
    .out_8(MAR_OUT));
  RAM #(.addrWidth(4), .bus("separate")) ram_1 (
    .addr(MAR_OUT), .din(in_4), .data({MSB, LSB}), .str(in_5), .clk(in_6), .ld(not_1_out), .clr(in_7));  // open: sel
  Instruction_Register instruction_register_1 (
    .in_3(Li_prime), .in_4(in_1), .in_5(in_8), .out_7(LSB), .out_8(MSB_3), .in_1(LSB), .in_2(MSB),
    .in_6(Ei_prime));
  CONTROLLER_2 controller_2_1 (
    .in_1(in_1), .in_2(in_9), .I7_I4(MSB_3), .HLT_prime(out_19), .Cp(Cp), .Ep(Ep), .LM_prime(LM_prime),
    .CE_prime(CE_prime), .Li_prime(Li_prime), .Ei_prime(Ei_prime), .LA_prime(LA_prime), .EA(EA), .Su(Su),
    .Eu(Eu), .LB_prime(LB_prime), .Lo_prime(Lo_prime));

  assign LSB_2 = LSB;
  assign LSB_3 = LSB;
  assign MAR_IN = LSB;
  assign MSB_2 = MSB;
  assign PC_OUT = LSB;

  // Other names for the same wires on the sheet: CLK = in_1

  // Notes on the sheet:
  //   RAM
  //   IR IN
  //   IR OUT
  //   LSB
  //   MSB
endmodule

module CONTROLLER_2 (
  input  in_1,
  input  in_2,
  input  [3:0] I7_I4,
  output HLT_prime,
  output Cp,
  output Ep,
  output LM_prime,
  output CE_prime,
  output Li_prime,
  output Ei_prime,
  output LA_prime,
  output EA,
  output Su,
  output Eu,
  output LB_prime,
  output Lo_prime
);

  wire and_1_out, and_2_out, and_3_out, and_4_out, and_5_out, and_6_out, and_7_out, and_8_out, and_9_out,
       and_10_out, and_11_out, and_12_out, and_13_out, and_14_out, and_15_out, and_16_out,
       instruction_decoder_1_add, instruction_decoder_1_hlt, instruction_decoder_1_lda,
       instruction_decoder_1_out, instruction_decoder_1_sub, nand_1_out, nand_2_out, or_1_out, or_2_out,
       or_3_out, or_4_out, or_6_out, T3, T4, T5, T6;

  Ring_counter_1_1 ring_counter_1_1_1 (.CLK(in_1), .CLR(in_2), .T1(Ep), .T2(Cp), .T3(T3), .T4(T4), .T5(T5), .T6(T6));
  Instruction_Decoder instruction_decoder_1 (
    .I7_I6_I5_I4(I7_I4), .LDA(instruction_decoder_1_lda), .ADD(instruction_decoder_1_add),
    .SUB(instruction_decoder_1_sub), .OUT(instruction_decoder_1_out), .HLT(instruction_decoder_1_hlt));
  not not_1 (HLT_prime, instruction_decoder_1_hlt);
  and and_1 (and_1_out, instruction_decoder_1_lda, T4);
  or or_1 (or_1_out, Ep, and_1_out, and_2_out, and_3_out);
  not not_2 (LM_prime, or_1_out);
  and and_2 (and_2_out, instruction_decoder_1_add, T4);
  and and_3 (and_3_out, instruction_decoder_1_sub, T4);
  and and_4 (and_4_out, instruction_decoder_1_lda, T5);
  or or_2 (or_2_out, T3, and_4_out, and_5_out, and_6_out);
  not not_3 (CE_prime, or_2_out);
  and and_5 (and_5_out, instruction_decoder_1_add, T5);
  and and_6 (and_6_out, instruction_decoder_1_sub, T5);
  not not_4 (Li_prime, T3);
  and and_7 (and_7_out, instruction_decoder_1_lda, T4);
  or or_3 (or_3_out, and_7_out, and_9_out, and_8_out);
  not not_5 (Ei_prime, or_3_out);
  and and_8 (and_8_out, instruction_decoder_1_sub, T4);
  and and_9 (and_9_out, instruction_decoder_1_add, T4);
  and and_10 (and_10_out, instruction_decoder_1_lda, T5);
  or or_4 (or_4_out, and_10_out, and_11_out, and_12_out);
  not not_6 (LA_prime, or_4_out);
  and and_11 (and_11_out, instruction_decoder_1_add, T6);
  and and_12 (and_12_out, instruction_decoder_1_sub, T6);
  nand nand_1 (nand_1_out, instruction_decoder_1_out, T4);
  not not_7 (EA, nand_1_out);
  nand nand_2 (nand_2_out, instruction_decoder_1_sub, T6);
  not not_8 (Su, nand_2_out);
  and and_13 (and_13_out, instruction_decoder_1_sub, T6);
  and and_14 (and_14_out, instruction_decoder_1_add, T6);
  or or_5 (Eu, and_14_out, and_13_out);
  and and_15 (and_15_out, instruction_decoder_1_add, T5);
  and and_16 (and_16_out, instruction_decoder_1_sub, T5);
  or or_6 (or_6_out, and_15_out, and_16_out);
  not not_9 (LB_prime, or_6_out);
  nand nand_3 (Lo_prime, instruction_decoder_1_out, T4);

  // Other names for the same wires on the sheet: T1 = Ep; T2 = Cp
endmodule

module sap_building_1_3_Organizing (
  input  in_1,
  input  in_2,
  output [3:0] LSB,
  output [3:0] MSB,
  output [3:0] out_5,
  output [3:0] out_6
);

  wire CE_prime, CLK, clock_1_out, Cp, EA, Ei_prime, Ep, Eu, HLT_prime, LA_prime, LB_prime, Li_prime,
       LM_prime, Lo_prime, not_1_out, Su;
  wire [3:0] A3_A0, A7_A4, B3_B0, B7_B4, IR_OUT_MSB, MAR_OUT;

  CONTROLLER controller_1 (
    .in_1(CLK), .in_2(in_2), .I7_I4(IR_OUT_MSB), .out_4(HLT_prime), .out_5(Cp), .out_6(Ep), .out_7(LM_prime),
    .out_8(CE_prime), .out_9(Li_prime), .out_10(Ei_prime), .out_11(LA_prime), .out_12(EA), .out_13(Su),
    .out_14(Eu), .out_15(LB_prime), .out_16(Lo_prime));
  prog__counter prog_counter_1 (.in_1(Cp), .in_2(CLK), .in_3(in_2), .in_4(Ep), .out_5(LSB));
  MAR mar_1 (
    .in_1(LSB[0]), .in_2(LSB[1]), .in_3(LSB[2]), .in_4(LSB[3]), .in_5(LM_prime), .in_6(CLK), .in_7(in_2),
    .out_8(MAR_OUT));
  not not_1 (not_1_out, CE_prime);
  Instruction_Register instruction_register_1 (
    .in_3(Li_prime), .in_4(CLK), .in_5(in_2), .out_7(LSB), .out_8(IR_OUT_MSB), .in_1(LSB), .in_2(MSB),
    .in_6(Ei_prime));
  RAM #(.addrWidth(4)) ram_1 (.addr(MAR_OUT), .data({MSB, LSB}), .ld(not_1_out), .clr(in_1));  // open: sel, clk
  Adder_Subtractor adder_subtractor_1 (
    .Su(Su), .B3B2B1B0(B3_B0), .A3A2A1A0(A3_A0), .B7B6B5B4(B7_B4), .A7A6A5A4(A7_A4), .out_7(LSB),
    .out_8(MSB), .in_6(Eu));  // open: out_9
  Accumulator_A accumulator_a_1 (
    .in_1(LSB), .in_2(MSB), .in_3(LA_prime), .in_4(CLK), .in_5(in_2), .in_6(EA), .out_7(LSB), .out_8(MSB),
    .out_9(A3_A0), .out_10(A7_A4));
  Register_B register_b_1 (
    .in_1(LSB), .in_2(MSB), .in_3(LB_prime), .in_4(CLK), .in_5(in_2), .out_6(B3_B0), .out_7(B7_B4));
  output_register output_register_1 (
    .in_1(LSB), .in_2(MSB), .in_3(Lo_prime), .in_4(CLK), .out_6(out_5), .out_7(out_6), .in_5(in_2));
  assign CLK = HLT_prime ? clock_1_out : 1'bz;  // Controlled_Buffer controlled_buffer_1
  Clock clock_1 (.out(clock_1_out));
  Hex_Digit_Display hex_digit_display_1 (.value(out_6));  // open: dp
  Hex_Digit_Display hex_digit_display_2 (.value(out_5));  // open: dp

  // Other names for the same wires on the sheet: A_IN_LSB[3:0] = LSB; A_OUT_LSB[3:0] = LSB; B_IN_LSB[3:0] = LSB;
  //   IR_IN_LSB[3:0] = LSB; IR_OUT_LSB[3:0] = LSB; MAR_IN[3:0] = LSB; O_IN_LSB[3:0] = LSB; PC_OUT[3:0] = LSB;
  //   RAM_OUT_LSB[3:0] = LSB; S3_S0[3:0] = LSB; A_IN_MSB[3:0] = MSB; A_OUT_MSB[3:0] = MSB; B_IN_MSB[3:0] = MSB;
  //   IR_IN_MSB[3:0] = MSB; O_IN_MSB[3:0] = MSB; RAM_OUT_MSB[3:0] = MSB; S7_S4[3:0] = MSB; CLR = in_2;
  //   O_OUT_LSB[3:0] = out_5; O_OUT_MSB[3:0] = out_6
endmodule

module Controller_Component (
  input  LDA,
  input  ADD,
  input  SUB,
  input  OUT,
  input  T1,
  input  T2,
  input  T3,
  input  T4,
  input  T5,
  input  T6,
  output Cp,
  output Ep,
  output LM_,
  output CE_,
  output Li_,
  output Ei_,
  output LA_,
  output EA,
  output Su,
  output Eu,
  output LB_,
  output Lo_
);

  wire nand_1_out, nand_2_out, nand_3_out, nand_4_out, nand_5_out, nand_6_out, nand_8_out, nand_9_out,
       nand_10_out, nand_11_out, nand_12_out, nand_13_out, nand_14_out, nand_15_out, nand_16_out,
       nand_18_out, nand_19_out, nand_20_out, nand_21_out, nand_23_out, nand_26_out, nand_27_out,
       nand_30_out, nand_31_out, nand_32_out, nand_33_out, nand_34_out, nand_36_out, nand_37_out,
       nand_38_out, nand_39_out, nand_40_out, nand_41_out, nand_43_out, nand_44_out;

  nand nand_1 (nand_1_out, T1, T1);
  nand nand_2 (nand_2_out, T4, T4);
  nand nand_3 (nand_3_out, T1, T1);
  nand nand_4 (nand_4_out, T3, T3);
  nand nand_5 (nand_5_out, T5, T5);
  nand nand_6 (nand_6_out, T3, T3);
  nand nand_7 (Li_, T3, T3);
  nand nand_8 (nand_8_out, OUT, OUT);
  nand nand_9 (nand_9_out, ADD, ADD);
  nand nand_10 (nand_10_out, SUB, SUB);
  nand nand_11 (nand_11_out, OUT, T4);
  nand nand_12 (nand_12_out, SUB, T6);
  nand nand_13 (nand_13_out, LDA, LDA);
  nand nand_14 (nand_14_out, OUT, OUT);
  nand nand_15 (nand_15_out, ADD, ADD);
  nand nand_16 (nand_16_out, SUB, SUB);
  nand nand_17 (Lo_, OUT, T4);
  nand nand_18 (nand_18_out, nand_1_out, nand_2_out);
  nand nand_19 (nand_19_out, OUT, nand_3_out);
  nand nand_20 (nand_20_out, nand_4_out, nand_5_out);
  nand nand_21 (nand_21_out, OUT, nand_6_out);
  nand nand_22 (Ei_, T4, nand_8_out);
  nand nand_23 (nand_23_out, nand_9_out, nand_10_out);
  nand nand_24 (EA, nand_11_out, nand_11_out);
  nand nand_25 (Su, nand_12_out, nand_12_out);
  nand nand_26 (nand_26_out, nand_13_out, nand_14_out);
  nand nand_27 (nand_27_out, nand_15_out, nand_16_out);
  nand nand_28 (LM_, nand_18_out, nand_19_out);
  nand nand_29 (CE_, nand_20_out, nand_21_out);
  nand nand_30 (nand_30_out, LDA, LDA);
  nand nand_31 (nand_31_out, T6, T6);
  nand nand_32 (nand_32_out, nand_23_out, nand_23_out);
  nand nand_33 (nand_33_out, T5, T5);
  nand nand_34 (nand_34_out, nand_26_out, nand_26_out);
  nand nand_35 (LB_, nand_27_out, T5);
  nand nand_36 (nand_36_out, nand_30_out, nand_31_out);
  nand nand_37 (nand_37_out, nand_32_out, nand_33_out);
  nand nand_38 (nand_38_out, nand_34_out, T6);
  nand nand_39 (nand_39_out, nand_36_out, nand_37_out);
  nand nand_40 (nand_40_out, T5, T5);
  nand nand_41 (nand_41_out, T6, T6);
  nand nand_42 (Eu, nand_38_out, nand_38_out);
  nand nand_43 (nand_43_out, nand_39_out, nand_39_out);
  nand nand_44 (nand_44_out, nand_40_out, nand_41_out);
  nand nand_45 (LA_, nand_43_out, nand_44_out);

  assign Cp = T2;
  assign Ep = T1;
endmodule

module instructions (
  input  LDA,
  input  ADD,
  input  SUB,
  input  OUT,
  input  T1,
  input  T2,
  input  T3,
  input  T4,
  input  T5,
  input  T6,
  output Cp,
  output Ep,
  output LM_,
  output CE_,
  output Li_,
  output Ei_,
  output LA_,
  output EA,
  output Su,
  output Eu,
  output LB_,
  output Lo_
);

  wire nand_1_out, nand_2_out, nand_3_out, nand_4_out, nand_5_out, nand_6_out, nand_8_out, nand_9_out,
       nand_10_out, nand_11_out, nand_12_out, nand_13_out, nand_14_out, nand_15_out, nand_16_out,
       nand_18_out, nand_19_out, nand_20_out, nand_21_out, nand_23_out, nand_26_out, nand_27_out,
       nand_30_out, nand_31_out, nand_32_out, nand_33_out, nand_34_out, nand_36_out, nand_37_out,
       nand_38_out, nand_39_out, nand_40_out, nand_41_out, nand_43_out, nand_44_out;

  nand nand_1 (nand_1_out, T1, T1);
  nand nand_2 (nand_2_out, T4, T4);
  nand nand_3 (nand_3_out, T1, T1);
  nand nand_4 (nand_4_out, T3, T3);
  nand nand_5 (nand_5_out, T5, T5);
  nand nand_6 (nand_6_out, T3, T3);
  nand nand_7 (Li_, T3, T3);
  nand nand_8 (nand_8_out, OUT, OUT);
  nand nand_9 (nand_9_out, ADD, ADD);
  nand nand_10 (nand_10_out, SUB, SUB);
  nand nand_11 (nand_11_out, OUT, T4);
  nand nand_12 (nand_12_out, SUB, T6);
  nand nand_13 (nand_13_out, LDA, LDA);
  nand nand_14 (nand_14_out, OUT, OUT);
  nand nand_15 (nand_15_out, ADD, ADD);
  nand nand_16 (nand_16_out, SUB, SUB);
  nand nand_17 (Lo_, OUT, T4);
  nand nand_18 (nand_18_out, nand_1_out, nand_2_out);
  nand nand_19 (nand_19_out, OUT, nand_3_out);
  nand nand_20 (nand_20_out, nand_4_out, nand_5_out);
  nand nand_21 (nand_21_out, OUT, nand_6_out);
  nand nand_22 (Ei_, T4, nand_8_out);
  nand nand_23 (nand_23_out, nand_9_out, nand_10_out);
  nand nand_24 (EA, nand_11_out, nand_11_out);
  nand nand_25 (Su, nand_12_out, nand_12_out);
  nand nand_26 (nand_26_out, nand_13_out, nand_14_out);
  nand nand_27 (nand_27_out, nand_15_out, nand_16_out);
  nand nand_28 (LM_, nand_18_out, nand_19_out);
  nand nand_29 (CE_, nand_20_out, nand_21_out);
  nand nand_30 (nand_30_out, LDA, LDA);
  nand nand_31 (nand_31_out, T6, T6);
  nand nand_32 (nand_32_out, nand_23_out, nand_23_out);
  nand nand_33 (nand_33_out, T5, T5);
  nand nand_34 (nand_34_out, nand_26_out, nand_26_out);
  nand nand_35 (LB_, nand_27_out, T5);
  nand nand_36 (nand_36_out, nand_30_out, nand_31_out);
  nand nand_37 (nand_37_out, nand_32_out, nand_33_out);
  nand nand_38 (nand_38_out, nand_34_out, T6);
  nand nand_39 (nand_39_out, nand_36_out, nand_37_out);
  nand nand_40 (nand_40_out, T5, T5);
  nand nand_41 (nand_41_out, T6, T6);
  nand nand_42 (Eu, nand_38_out, nand_38_out);
  nand nand_43 (nand_43_out, nand_39_out, nand_39_out);
  nand nand_44 (nand_44_out, nand_40_out, nand_41_out);
  nand nand_45 (LA_, nand_43_out, nand_44_out);

  assign Cp = T2;
  assign Ep = T1;
endmodule

module testing_field_3 (
);

  CONTROLLER controller_1 ();  // open: in_1, in_2, I7_I4, out_4, out_5, out_6, out_7, out_8, out_9, out_10, out_11, out_12, out_13, out_14, out_15, out_16
  Controller_Component controller_component_1 ();  // open: LDA, ADD, SUB, OUT, T1, T2, T3, T4, T5, T6, Cp, Ep, LM_, CE_, Li_, Ei_, LA_, EA, Su, Eu, LB_, Lo_
endmodule

module CONTROLLER (
  input  in_1,
  input  in_2,
  input  [3:0] I7_I4,
  output out_4,
  output out_5,
  output out_6,
  output out_7,
  output out_8,
  output out_9,
  output out_10,
  output out_11,
  output out_12,
  output out_13,
  output out_14,
  output out_15,
  output out_16
);

  wire instruction_decoder_1_add, instruction_decoder_1_hlt, instruction_decoder_1_lda,
       instruction_decoder_1_out, instruction_decoder_1_sub, T1, T2, T3, T4, T5, T6;

  Ring_counter_1_1 ring_counter_1_1_1 (.CLK(in_1), .CLR(in_2), .T1(T1), .T2(T2), .T3(T3), .T4(T4), .T5(T5), .T6(T6));
  Instruction_Decoder instruction_decoder_1 (
    .I7_I6_I5_I4(I7_I4), .LDA(instruction_decoder_1_lda), .ADD(instruction_decoder_1_add),
    .SUB(instruction_decoder_1_sub), .OUT(instruction_decoder_1_out), .HLT(instruction_decoder_1_hlt));
  not not_1 (out_4, instruction_decoder_1_hlt);
  Controller_Component controller_component_1 (
    .LDA(instruction_decoder_1_lda), .ADD(instruction_decoder_1_add), .SUB(instruction_decoder_1_sub),
    .OUT(instruction_decoder_1_out), .T1(T1), .T2(T2), .T3(T3), .T4(T4), .T5(T5), .T6(T6), .Cp(out_5),
    .Ep(out_6), .LM_(out_7), .CE_(out_8), .Li_(out_9), .Ei_(out_10), .LA_(out_11), .EA(out_12), .Su(out_13),
    .Eu(out_14), .LB_(out_15), .Lo_(out_16));
endmodule
